# Fritzing sketch wheelchaircontrollerfzz (saved by Fritzing 1.0.2b)
breadboards: 1
perfboards: 1

parts:
  Part1 = Arduino Due (Rev2b)
  Part3 = LCD1602-I2C
  J3 = AVR ISP 6 Pin [package=2x3_lock]
  M1 = MPS20N0040D
  A2 = USB A power source  # not connected

nets:
  N1: Part1.D14/TX3, J3.2
  N2: Part1.D15/RX3, J3.1
  N3: Part1.D20/SDA3, Part3.SDA
  N4: Part1.D21/SCL3, Part3.SCL
  N5: Part1.D6_PWM, M1.OUT
  N6: Part1.D7_PWM, M1.SCK

custom parts:
  LCD1602-I2C: A standard character display, usually with 2x16 characters. Comes in many colors with LCM1602 IIC attached.
  MPS20N0040D: MPS20N0040D Sphygmomanometer 0-40kPa Differential Air Pressure Sensor / HX710B ADC Module This module couples a MPS20N0040D sphygmomanometer air pressure sensor module with an HX710B analog-to-digital converter IC. It can be powered from a 3.3V or 5V source, with a claimed measurement range of 0-40kPa. It uses a proprietary 2-wire communication protocol and is thus not I2C compatible. Links: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
  USB A power source: USB A power source.
